# Fritzing sketch Kiln Mains Board (saved by Fritzing 1.0.7)

parts:
  J1_240VAC_IN = Terminal block 2p 7.62mm (41A) in [value="41A block" package=THT]
  K1 = TE T92S7D22-12 relay (DPST-NO 30A, 12VDC coil) [value=T92S7D22-12 mn="TE Connectivity" part_number=T92S7D22-12 package=THT]
  J3_SSR_LOAD = Terminal block 2p 7.62mm (41A) [value="41A block" package=THT]
  J2_KILN_OUT = Terminal block 2p 7.62mm (41A) [value="41A block" package=THT]
  F1 = FUSE [value="500mA T" package=fuse_5mm]
  MOV1 = Metal oxide varistor 275VAC (14mm disc) [value=S14K275 part_number=S14K275 package="THT radial"]
  PS1 = Mean Well IRM-20-12 (20W 12V PCB AC-DC) [value=IRM-20-12 mn="Mean Well" part_number=IRM-20-12 package=THT]
  VR1 = Traco TSR 2-2450 (5V 2A switching regulator, SIP3) [value="TSR 2-2450" mn="Traco Power" part_number="TSR 2-2450" package=THT]
  C1 = Electrolytic Capacitor [value="10uF 25V" capacitance=1µF voltage=35V package="100 mil [THT, electrolytic]"]
  C3 = Ceramic Capacitor [value=100nF capacitance=100nF package="100 mil [THT, multilayer]"]
  C2 = Electrolytic Capacitor [value="10uF 16V" capacitance=1µF package="100 mil [THT, electrolytic]"]
  C4 = Ceramic Capacitor [value=100nF capacitance=100nF package="100 mil [THT, multilayer]"]
  J5_THERMAL_NC = Terminal block 2p 5.08mm in [package=THT]
  RLY1 = RELAY [value="12V SPST" package=relay-g5q]
  D1 = Rectifier Diode [value=1N4007 part_number=1N4001 package="300 mil [THT]"]
  Q1 = Basic FET N-Channel [value=IRLZ44N package="TO220 [THT]"]
  R8 = Resistor [value=1k tolerance=±5% power=0.25W resistance=220 package=THT]
  LED2_CTX = LED - 5mm [value=green color="Red (633nm)" current=0.030A package="5 mm [THT]"]
  J6C_PI_EN/AUX = Terminal block 2p 5.08mm in [package=THT]
  D2 = Rectifier Diode [value=1N4148 part_number=1N4001 package="300 mil [THT]"]
  R3 = Resistor [value=100R tolerance=±5% power=0.25W resistance=220 package=THT]
  R4 = Resistor [value=10k tolerance=±5% power=0.25W resistance=220 package=THT]
  Q2 = Basic FET N-Channel [value=2N7000 package="TO220 [THT]"]
  J6B_PI_CTX/HEAT = Terminal block 2p 5.08mm in [package=THT]
  R1 = Resistor [value=100R tolerance=±5% power=0.25W resistance=220 package=THT]
  R2 = Resistor [value=10k tolerance=±5% power=0.25W resistance=220 package=THT]
  R5 = Resistor [value=100R tolerance=±5% power=0.25W resistance=220 package=THT]
  R6 = Resistor [value=10k tolerance=±5% power=0.25W resistance=220 package=THT]
  Q3 = Basic FET N-Channel [value=2N7000 package="TO220 [THT]"]
  R7 = Resistor [value=1k tolerance=±5% power=0.25W resistance=220 package=THT]
  LED1_HEAT = LED - 5mm [value=red color="Red (633nm)" current=0.030A package="5 mm [THT]"]
  J4_SSR_DRIVE = Terminal block 2p 5.08mm [package=THT]
  J6A_PI_5V/GND = Terminal block 2p 5.08mm in [package=THT]
  R9 = Resistor [value=1k tolerance=±5% power=0.25W resistance=220 package=THT]
  LED3_PWR = LED - 5mm [value=green color="Red (633nm)" current=0.030A package="5 mm [THT]"]
  J7_FAN_12V = Terminal block 2p 5.08mm in [package=THT]

nets:
  N1: J1_240VAC_IN.1, K1.2a, K1.2b, F1.1
  N2: J1_240VAC_IN.2, K1.6a, K1.6b, MOV1.2, PS1.AC/N
  N3: K1.4a, K1.4b, J3_SSR_LOAD.1
  N4: K1.8a, K1.8b, J2_KILN_OUT.2
  N5: K1.A1a, K1.A1b, RLY1.NO, D1.cathode, R8.Pin_0
  N6: K1.A2a, K1.A2b, D1.anode, Q1.drain, LED2_CTX.cathode
  N7: J3_SSR_LOAD.2, J2_KILN_OUT.1
  N8: F1.2, MOV1.1, PS1.AC/L
  12V: PS1.+V, VR1.+Vin, C1.+, C3.0, J5_THERMAL_NC.1, RLY1.COIL1, D2.cathode, J7_FAN_12V.1
  GND: PS1.-V, VR1.GND, C1.-, C3.1, C2.-, C4.1, Q1.source, R4.Pin_1, Q2.source, R2.Pin_1, R6.Pin_1, Q3.source, J6A_PI_5V/GND.2, LED3_PWR.cathode, J7_FAN_12V.2
  5V: VR1.+Vout, C2.+, C4.0, R7.Pin_0, J4_SSR_DRIVE.1, J6A_PI_5V/GND.1, R9.Pin_0
  N9: J5_THERMAL_NC.2, RLY1.MAIN
  N10: RLY1.COIL2, D2.anode, Q2.drain
  N11: Q1.gate, R1.Pin_1, R2.Pin_0
  N12: R8.Pin_1, LED2_CTX.anode
  N13: J6C_PI_EN/AUX.1, R3.Pin_0
  N14: R3.Pin_1, R4.Pin_0, Q2.gate
  N15: J6B_PI_CTX/HEAT.1, R1.Pin_0
  N16: J6B_PI_CTX/HEAT.2, R5.Pin_0
  N17: R5.Pin_1, R6.Pin_0, Q3.gate
  N18: Q3.drain, LED1_HEAT.cathode, J4_SSR_DRIVE.2
  N19: R7.Pin_1, LED1_HEAT.anode
  N20: R9.Pin_1, LED3_PWR.anode

custom parts:
  Terminal block 2p 7.62mm (41A) in: As TB2_762_kilnmains but drawn with its schematic pins on the right, for terminals that feed the sheet from the left edge.
  TE T92S7D22-12 relay (DPST-NO 30A, 12VDC coil): TE / Potter & Brumfield T92 two-pole 30 A PCB relay, 2 form A, 12 VDC coil. Each terminal is two 1.93 mm holes on 5.16 mm centres (a and b) - BOTH must be connected, they are one terminal. Footprint from TE datasheet 1308242 rev 1217, termination code 1.
  Terminal block 2p 7.62mm (41A): Two-position PCB terminal block on 7.62 mm pitch rated 41 A / 10 mm2 (Phoenix Contact PC 5 series or equivalent). Use for every mains connection on this board - the 5 mm blocks in the Fritzing core top out around 16 A.
  Metal oxide varistor 275VAC (14mm disc): 275 VAC-rated metal oxide varistor across the PSU input, 14 mm disc on 7.5 mm lead pitch (TDK S14K275, Littelfuse V275LA20AP or equivalent). Fit it downstream of F1 so a failed MOV blows the fuse rather than the branch circuit breaker.
  Mean Well IRM-20-12 (20W 12V PCB AC-DC): Mean Well IRM-20-12 encapsulated PCB-mount AC-DC module. 85-264 VAC universal input (non-polarised, so L1-L2 at 240 V is fine), 12 V 1.8 A out, convection cooled, Class II. Footprint from Mean Well case 219A (datasheet bottom view, mirrored here to a top-down footprint).
  Traco TSR 2-2450 (5V 2A switching regulator, SIP3): Traco TSR 2-2450 non-isolated buck regulator, 7805 pinout, 5 V 2 A, no heatsink needed. Footprint from the TSR 2 series outline drawing.
  Terminal block 2p 5.08mm in: As TB2_508_kilnmains but with its schematic pins on the right, for terminals that feed the sheet from the left edge.
  Terminal block 2p 5.08mm: Two-position PCB terminal block on 5.08 mm pitch, for the SELV side (Pi interface, SSR drive, thermal switch, fan).
