# Fritzing sketch Kiln Controller (saved by Fritzing 1.0.7)
circuit board: 6.50001cm x 5.65cm
circuit board: 5.48459cm x 3.29972cm
breadboards: 3

parts:
  EMRG = Screw terminal - 2 pins [package=THT]
  Arduino_Metro_Mini = Adafruit Metro Mini [part_number="Adafruit #2590"]
  Q2 = NPN-Transistor [package="SOT-23 [SMD]"]
  DOOR = smd LED [color="Green (570nm)" current=0.030 package="0805 [SMD]"]
  RUN = smd LED [color="Green (570nm)" current=0.030 package="0805 [SMD]"]
  SAFE = smd LED [color="Green (570nm)" current=0.030 package="0805 [SMD]"]
  EMRG_2 = smd LED [color="Green (570nm)" current=0.030 package="0805 [SMD]"]
  DOOR_2 = Screw terminal - 2 pins [package=THT]
  HEAT = smd LED [color="Red (633nm)" current=0.030 package="0805 [SMD]"]
  Q1 = NPN-Transistor [package="SOT-23 [SMD]"]
  TC-Safe = Screw terminal - 2 pins [package=THT]
  Raspberry_Pi_1 = Raspberry Pi 3 [part_number=RPI-3-V1.2]
  R1 = Resistor [tolerance=±5% resistance=47k power=0.25 package="0805 [SMD]"]
  C3 = Ceramic Capacitor [capacitance=10nF voltage=35V package="0805 [SMD, multilayer]"]
  IC2 = SO08-EIAJ [chip_label=MAX31855K package=SO]
  C2 = Ceramic Capacitor [capacitance=0.1µF voltage=35V package="0805 [SMD, multilayer]"]
  SW-POWER = Screw terminal - 2 pins [package=THT]
  TC-PRI = Screw terminal - 2 pins [package=THT]
  STAT = smd LED [color="Red (633nm)" current=0.030 package="0805 [SMD]"]
  U5 = TLP291-4 (SOP16 SMD) [part_number=TLP291-4 package="SOP16 [SMD]"]
  IC1 = SO08-EIAJ [chip_label=MAX31855K package=SO]
  C1 = Ceramic Capacitor [capacitance=0.1µF voltage=35V package="0805 [SMD, multilayer]"]
  J1 = JST-XH_2.54mm Horizontal SMD Connector 8pin [package=SMD]
  C4 = Ceramic Capacitor [capacitance=10nF voltage=35V package="0805 [SMD, multilayer]"]
  J5 = double row male pin header, 10 pins [form="♂ (male)"]
  J3 = JST XH_2.54mm Horizontal SMD Connector 3pin [package=SMD]
  J2 = JST-XH_2.54mm Horizontal SMD Connector 8pin [package=SMD]
  J4 = JST XH_2.54mm Horizontal SMD Connector 3pin [package=SMD]
  R11 = Resistor [tolerance=±5% resistance=390 power=0.25 package="0805 [SMD]"]
  R10 = Resistor [tolerance=±5% resistance=390 power=0.25 package="0805 [SMD]"]
  R7 = Resistor [tolerance=±5% resistance=390 power=0.25 package="0805 [SMD]"]
  R6 = Resistor [tolerance=±5% resistance=390 power=0.25 package="0805 [SMD]"]
  R8 = Resistor [tolerance=±5% resistance=390 power=0.25 package="0805 [SMD]"]
  R9 = Resistor [tolerance=±5% resistance=390 power=0.25 package="0805 [SMD]"]

nets:
  N1: EMRG.pin1, U5.A3, J3.pin2, J4.pin2
  5V: EMRG.pin2, Arduino_Metro_Mini.+5V, Q2.1, DOOR_2.pin2, Raspberry_Pi_1.5V, IC2.4, C2.1, U5.C1, IC1.4, C1.1, J1.pin1, J5.pin2, J5.pin3, J5.pin7, J5.pin8, J5.pin9, J2.pin1
  N2: Arduino_Metro_Mini.AD5/SCL, Raspberry_Pi_1.GPIO3, SW-POWER.pin2, J3.pin1, J4.pin1
  N3: Arduino_Metro_Mini.AD4/SDA, Raspberry_Pi_1.GPIO2
  N4: Arduino_Metro_Mini.IO12, U5.A2
  N5: Arduino_Metro_Mini.IO4, IC1.5
  N6: Arduino_Metro_Mini.IO3, IC1.6
  N7: Arduino_Metro_Mini.IO2, IC1.7
  N8: Arduino_Metro_Mini.RESET, Raspberry_Pi_1.GPIO10
  GND: Arduino_Metro_Mini.GND, DOOR.cathode, RUN.cathode, SAFE.cathode, EMRG_2.cathode, HEAT.cathode, Q1.2, Raspberry_Pi_1.GND, IC2.1, C2.0, SW-POWER.pin1, STAT.cathode, IC1.1, C1.0, J1.pin2, J5.pin1, J5.pin6, J5.pin10, J2.pin2
  N9: Q2.2, J5.pin4
  N10: Q2.0, R1.Pin_1
  N11: DOOR.anode, R11.Pin_1
  N12: RUN.anode, R6.Pin_1
  N13: SAFE.anode, R7.Pin_1
  N14: EMRG_2.anode, R10.Pin_1
  N15: DOOR_2.pin1, U5.A4, J3.pin3, J4.pin3
  N16: HEAT.anode, R8.Pin_1
  N17: Q1.0, U5.E4
  N18: Q1.1, J5.pin5
  N19: TC-Safe.pin1, C3.1, IC2.3
  N20: TC-Safe.pin2, C3.0, IC2.2
  N21: Raspberry_Pi_1.GPIO17, IC2.7
  N22: Raspberry_Pi_1.GPIO27, IC2.6
  N23: Raspberry_Pi_1.GPIO22, IC2.5
  N24: Raspberry_Pi_1.GPIO9, U5.A1
  N25: Raspberry_Pi_1.GPIO11, R1.Pin_0
  N26: Raspberry_Pi_1.GPIO26, J1.pin8, J2.pin8, R9.Pin_0
  N27: TC-PRI.pin1, IC1.3, C4.1
  N28: TC-PRI.pin2, IC1.2, C4.0
  N29: STAT.anode, R9.Pin_1
  N30: U5.K1, J1.pin6, J2.pin6, R6.Pin_0
  N31: U5.K2, J1.pin5, J2.pin5, R7.Pin_0
  N32: U5.K3, J1.pin4, J2.pin4, R10.Pin_0
  N33: U5.K4, J1.pin3, J2.pin3, R11.Pin_0
  N34: U5.C4, U5.E3
  N35: U5.C3, U5.E2
  N36: U5.C2, U5.E1
  N37: J1.pin7, J2.pin7, R8.Pin_0

notes:
  ylw
  red
  Adafruit Metro Mini
  TC-PRI
  TC-SAF
  Kiln Controller
  PiHat v2.1
  CTX
  HEAT
  +5V
  GND

custom parts:
  Adafruit Metro Mini: We sure love the ATmega328 here at Adafruit, and we use them a lot for our own projects. The processor has plenty of GPIO, Analog inputs, hardware UART SPI and I2C, timers and PWM galore - just enough for most simple projects. When we need to go small, we use a Pro Trinket 3V or 5V, but if you want to have USB-to-Serial built in, we reach for an Adafruit METRO Mini. METRO Mini is the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
  TLP291-4 (SOP16 SMD): Toshiba TLP291-4 quad photocoupler on a DIP-16 compatible breakout carrier. Breadboard view is the breakout module (0.1in pitch, 0.3in row spacing) so it plugs into a breadboard. PCB view is the bare SOP16 SMD land pattern from datasheet section 13: pad 0.8 x 1.2mm, 1.27mm pitch, 6.3mm between pad-row centres. Use this variant when you solder the bare chip to your board.
  JST-XH_2.54mm Horizontal SMD Connector 8pin: JST-XH_2.54mm Horizontal SMD Connector 8pin.
  JST XH_2.54mm Horizontal SMD Connector 3pin: JST XH_2.54mm Horizontal SMD Connector 3pin.
